// Digital circuit Branch_Unit.dig as structural Verilog
module Branch_Unit (
  input  isUBranch,
  input  isBEQ,
  input  flags_E_54bb86e1,
  input  isBgt,
  input  flags_gt_19528b5f,
  output isBrachTaken
);

  wire and_1_out, and_2_out;

  and and_1 (and_1_out, isBEQ, flags_E_54bb86e1);
  and and_2 (and_2_out, isBgt, flags_gt_19528b5f);
  or or_1 (isBrachTaken, isUBranch, and_1_out, and_2_out);
endmodule
