// Digital circuit Data_Lck.dig as structural Verilog
module Data_Lck (
  input  [31:0] IF_0F_263986f9,
  input  [31:0] OF_EX_fa6b6bb9,
  output Data_Lock_Conflict_b6a1ac3c
);

  wire and_1_out, and_2_out, and_3_out, check_opcode1_1_s, check_opcode2_1_s, compare_1_s, compare_2_s,
       nand_1_out, or_1_out;

  check_opcode1 check_opcode1_1 (.A(IF_0F_263986f9[4:0]), .S(check_opcode1_1_s));
  and and_1 (and_1_out, ~OF_EX_fa6b6bb9[28], 1'b1);  // And
  nand nand_1 (nand_1_out, IF_0F_263986f9[0], 1'b1);
  compare compare_1 (.A(IF_0F_263986f9[21:18]), .B(OF_EX_fa6b6bb9[25:22]), .S(compare_1_s));
  and and_2 (and_2_out, compare_1_s, check_opcode1_1_s);
  and and_3 (and_3_out, check_opcode2_1_s, compare_2_s);
  or or_1 (or_1_out, and_3_out, and_2_out);
  compare compare_2 (.A(IF_0F_263986f9[17:14]), .B(OF_EX_fa6b6bb9[25:22]), .S(compare_2_s));
  and and_4 (Data_Lock_Conflict_b6a1ac3c, or_1_out, and_1_out, nand_1_out);
  check_opcode2 check_opcode2_1 (.A(IF_0F_263986f9[4:0]), .S(check_opcode2_1_s));
endmodule
