// Digital circuit EX_MA.dig as structural Verilog
module EX_MA (
  input  [31:0] PC,
  input  [31:0] aluR,
  input  [31:0] op2,
  input  [31:0] instr,
  input  clkIn,
  input  isld,
  input  isst,
  input  iscall,
  input  iswb,
  output [31:0] PC_out,
  output [31:0] aluR_out,
  output [31:0] op2_out,
  output [31:0] instr_out,
  output iswb_o,
  output iscall_o,
  output isst_o,
  output isld_o,
  output [31:0] instr_out2
);

  Register #(.Bits(32)) register_1 (.D(PC), .C(clkIn), .en(1'b1), .Q(PC_out));
  Register #(.Bits(32)) register_2 (.D(aluR), .C(clkIn), .en(1'b1), .Q(aluR_out));
  Register #(.Bits(32)) register_3 (.D(op2), .C(clkIn), .en(1'b1), .Q(op2_out));
  Register #(.Bits(32)) register_4 (.D(instr), .C(clkIn), .en(1'b1), .Q(instr_out));
  Register register_5 (.D(isld), .C(clkIn), .en(1'b1), .Q(isld_o));
  Register register_6 (.D(isst), .C(clkIn), .en(1'b1), .Q(isst_o));
  Register register_7 (.D(iscall), .C(clkIn), .en(1'b1), .Q(iscall_o));
  Register register_8 (.D(iswb), .C(clkIn), .en(1'b1), .Q(iswb_o));

  assign instr_out2 = instr_out;
endmodule
