// Digital circuit Memory_Unit.dig as structural Verilog
module Memory_Unit (
  input  [31:0] MAR,
  input  [31:0] MDR,
  input  isSt,
  input  isLd,
  input  Clk,
  output [31:0] IdResult
);

  RAMDualPort #(.AddrBits(24), .Bits(32)) ramdualport_1 (
    .A(MAR[25:2]), .Din(MDR), .str(isSt), .C(Clk), .ld(isLd), .D(IdResult));
endmodule
