// Digital circuit OF_EX.dig as structural Verilog
module OF_EX (
  input  [31:0] PC,
  input  [31:0] brantgt,
  input  [31:0] B,
  input  [31:0] A,
  input  [31:0] OP2,
  input  [31:0] Inst,
  input  clkIn,
  input  isWb,
  input  bubble,
  input  isCall,
  input  isSt,
  input  isLd,
  input  isUbranch,
  input  isBgt,
  input  [12:0] ALU_signals,
  input  isBeq,
  input  isRet,
  output [31:0] PC_out,
  output [31:0] brantgt_out,
  output [31:0] B_out,
  output [31:0] A_out,
  output [31:0] OP2_out,
  output [31:0] Inst_out,
  output [31:0] Inst_out2,
  output [12:0] aluSignals_out,
  output isret_out,
  output isbeq_out,
  output isgbt_out,
  output isub_out,
  output isld_out,
  output isst_out,
  output iscal_out,
  output iswb_out
);

  wire [31:0] multiplexer_1_out;

  Register #(.Bits(32)) register_1 (.D(PC), .C(clkIn), .en(1'b1), .Q(PC_out));
  Register #(.Bits(32)) register_2 (.D(brantgt), .C(clkIn), .en(1'b1), .Q(brantgt_out));
  Register #(.Bits(32)) register_3 (.D(B), .C(clkIn), .en(1'b1), .Q(B_out));
  Register #(.Bits(32)) register_4 (.D(A), .C(clkIn), .en(1'b1), .Q(A_out));
  Register #(.Bits(32)) register_5 (.D(OP2), .C(clkIn), .en(1'b1), .Q(OP2_out));
  Multiplexer #(.Bits(32)) multiplexer_1 (.sel(bubble), .in_0(Inst), .in_1(OP2_out), .out(multiplexer_1_out));
  Register #(.Bits(32)) register_6 (.D(multiplexer_1_out), .C(clkIn), .en(1'b1), .Q(Inst_out));
  controlpkt controlpkt_1 ();

  assign Inst_out2 = Inst_out;
endmodule
