// Digital circuit check_opcode1.dig as structural Verilog
module check_opcode1 (
  input  [4:0] A,
  output S
);

  wire and_1_out, and_2_out, and_3_out;

  and and_1 (and_1_out, ~A[2], ~A[3], A[4]);  // And
  and and_2 (and_2_out, A[0], ~A[4]);  // And
  nor nor_1 (S, and_3_out, and_2_out, and_1_out);
  and and_3 (and_3_out, ~A[1], A[3], ~A[4]);  // And
endmodule
