// Digital circuit compare.dig as structural Verilog
module compare (
  input  [3:0] A,
  input  [3:0] B,
  output S
);

  wire [3:0] sub_1_s;

  Sub #(.Bits(4)) sub_1 (.a(A), .b(B), .c_i(1'b0), .s(sub_1_s));  // open: c_o
  nor nor_1 (S, sub_1_s[0], sub_1_s[1], sub_1_s[2], sub_1_s[3]);
endmodule
