// Digital circuit conflit-detection-unit.dig as structural Verilog
module conflit_detection_unit (
  input  [31:0] A,
  input  [31:0] B,
  output FO_conflict,
  output SO_conflict
);

  wire and_1_out, and_2_out, and_3_out, check_opa_op1_1_o, check_opa_op2_1_o, check_opb_1_o, comparator_1_eq,
       comparator_2_eq, instruction_split_a_1_has_src2;
  wire [3:0] instruction_split_a_1_src1, instruction_split_a_1_src2, instruction_split_b_1_dest;

  check_opA_op1 check_opa_op1_1 (.I(A[31:27]), .O(check_opa_op1_1_o));
  check_opA_op2 check_opa_op2_1 (.I(A[31:27]), .O(check_opa_op2_1_o));
  and and_1 (and_1_out, check_opb_1_o, check_opa_op1_1_o);
  and and_2 (and_2_out, check_opb_1_o, check_opa_op2_1_o);
  instruction_split_A instruction_split_a_1 (
    .opA(A[31:27]), .opA_A(A[26:0]), .src1(instruction_split_a_1_src1),
    .has_src2(instruction_split_a_1_has_src2), .src2(instruction_split_a_1_src2));
  check_opB check_opb_1 (.I(B[31:27]), .O(check_opb_1_o));
  Multiplexer multiplexer_1 (.sel(and_1_out), .in_0(1'b0), .in_1(comparator_1_eq), .out(FO_conflict));
  Comparator #(.Bits(4)) comparator_1 (
    .a(instruction_split_b_1_dest), .b(instruction_split_a_1_src1), .eq(comparator_1_eq));  // open: gt, lt
  and and_3 (and_3_out, comparator_2_eq, instruction_split_a_1_has_src2);
  Multiplexer multiplexer_2 (.sel(and_2_out), .in_0(1'b0), .in_1(and_3_out), .out(SO_conflict));
  instruction_split_b instruction_split_b_1 (.opB_5(B[31:27]), .opB_27(B[26:0]), .dest(instruction_split_b_1_dest));
  Comparator #(.Bits(4)) comparator_2 (
    .a(instruction_split_b_1_dest), .b(instruction_split_a_1_src2), .eq(comparator_2_eq));  // open: gt, lt
endmodule
