// Digital circuit control_unit.dig as structural Verilog
module control_unit (
  input  [4:0] opcode,
  input  in_3,
  output isSt,
  output isImm,
  output isLd,
  output isBeq,
  output isBgt,
  output isRet,
  output isWb,
  output isUbranch,
  output isCall,
  output [12:0] SinalULA
);

  wire and_1_out, and_7_out, and_8_out, and_9_out, and_10_out, and_11_out, and_13_out, and_14_out, not_1_out,
       not_2_out, not_3_out, not_4_out, not_5_out, not_6_out, not_7_out, not_8_out, not_9_out, not_10_out,
       not_11_out, not_12_out, not_13_out, not_14_out, not_15_out, not_16_out, not_17_out, not_18_out,
       not_19_out, not_20_out, not_22_out, not_23_out, not_24_out, not_25_out, not_26_out, not_27_out,
       not_28_out, not_29_out, not_30_out, not_31_out, not_32_out, not_33_out, not_34_out, not_35_out,
       not_36_out, not_37_out, not_38_out, not_39_out, not_40_out, not_41_out, not_42_out, not_43_out,
       not_44_out, not_45_out, not_46_out, not_47_out, not_48_out, not_49_out, not_50_out, not_51_out,
       not_52_out, not_53_out, not_54_out, not_55_out, not_56_out, not_57_out, not_58_out, not_59_out,
       not_60_out, not_61_out, not_62_out, not_63_out, not_64_out, not_65_out, not_66_out, not_67_out,
       not_68_out, not_69_out;

  and and_1 (and_1_out, opcode[0], opcode[1]);
  not not_1 (not_1_out, and_1_out);
  not not_2 (not_2_out, opcode[4]);
  not not_3 (not_3_out, opcode[0]);
  not not_4 (not_4_out, opcode[4]);
  not not_5 (not_5_out, opcode[0]);
  not not_6 (not_6_out, opcode[1]);
  not not_7 (not_7_out, opcode[2]);
  not not_8 (not_8_out, opcode[3]);
  not not_9 (not_9_out, opcode[1]);
  not not_10 (not_10_out, opcode[2]);
  not not_11 (not_11_out, opcode[3]);
  not not_12 (not_12_out, opcode[0]);
  not not_13 (not_13_out, opcode[1]);
  not not_14 (not_14_out, opcode[3]);
  not not_15 (not_15_out, opcode[1]);
  not not_16 (not_16_out, opcode[4]);
  not not_17 (not_17_out, opcode[4]);
  not not_18 (not_18_out, opcode[1]);
  not not_19 (not_19_out, opcode[3]);
  not not_20 (not_20_out, opcode[0]);
  not not_21 (not_20_out, opcode[0]);
  not not_22 (not_22_out, opcode[1]);
  not not_23 (not_23_out, opcode[3]);
  not not_24 (not_24_out, opcode[2]);
  not not_25 (not_25_out, opcode[3]);
  not not_26 (not_26_out, opcode[0]);
  not not_27 (not_27_out, opcode[1]);
  not not_28 (not_28_out, opcode[2]);
  not not_29 (not_29_out, opcode[3]);
  not not_30 (not_30_out, opcode[4]);
  not not_31 (not_31_out, opcode[4]);
  not not_32 (not_32_out, opcode[1]);
  not not_33 (not_33_out, opcode[2]);
  not not_34 (not_34_out, opcode[3]);
  not not_35 (not_35_out, opcode[4]);
  not not_36 (not_36_out, opcode[1]);
  not not_37 (not_37_out, opcode[3]);
  not not_38 (not_38_out, opcode[4]);
  not not_39 (not_39_out, opcode[0]);
  not not_40 (not_40_out, opcode[2]);
  not not_41 (not_41_out, opcode[3]);
  not not_42 (not_42_out, opcode[4]);
  not not_43 (not_43_out, opcode[2]);
  not not_44 (not_44_out, opcode[3]);
  not not_45 (not_45_out, opcode[4]);
  not not_46 (not_46_out, opcode[0]);
  not not_47 (not_47_out, opcode[1]);
  not not_48 (not_48_out, opcode[3]);
  not not_49 (not_49_out, opcode[4]);
  not not_50 (not_50_out, opcode[0]);
  not not_51 (not_51_out, opcode[2]);
  not not_52 (not_52_out, opcode[4]);
  not not_53 (not_53_out, opcode[2]);
  not not_54 (not_54_out, opcode[4]);
  not not_55 (not_55_out, opcode[0]);
  not not_56 (not_56_out, opcode[1]);
  not not_57 (not_57_out, opcode[4]);
  not not_58 (not_58_out, opcode[3]);
  not not_59 (not_59_out, opcode[4]);
  not not_60 (not_60_out, opcode[0]);
  not not_61 (not_61_out, opcode[3]);
  not not_62 (not_62_out, opcode[4]);
  not not_63 (not_63_out, opcode[0]);
  not not_64 (not_64_out, opcode[1]);
  not not_65 (not_65_out, opcode[2]);
  not not_66 (not_66_out, opcode[4]);
  not not_67 (not_67_out, opcode[1]);
  not not_68 (not_68_out, opcode[2]);
  not not_69 (not_69_out, opcode[4]);
  and and_2 (isSt, opcode[0], opcode[1], opcode[2], opcode[3], not_2_out);
  // And and_3 has open pins: In_1=not_3_out, In_2=opcode[1], In_3=opcode[2], In_4=opcode[3], In_5=not_4_out, out=open
  // And and_4 has open pins: In_1=not_5_out, In_2=not_6_out, In_3=not_7_out, In_4=not_8_out, In_5=opcode[4], out=open
  // And and_5 has open pins: In_1=opcode[0], In_2=not_9_out, In_3=not_10_out, In_4=not_11_out, In_5=opcode[4], out=open
  // And and_6 has open pins: In_1=not_12_out, In_2=not_13_out, In_3=opcode[2], In_4=not_14_out, In_5=opcode[4], out=open
  and and_7 (and_7_out, opcode[0], not_15_out, opcode[2], not_16_out);
  and and_8 (and_8_out, opcode[0], opcode[2], opcode[3], not_17_out);
  and and_9 (and_9_out, opcode[4], not_1_out);
  and and_10 (and_10_out, opcode[1], not_18_out, not_19_out, opcode[4]);
  and and_11 (and_11_out, not_20_out, not_22_out, opcode[2], not_23_out, opcode[4]);
  and and_12 (isCall, opcode[0], opcode[1], not_24_out, not_25_out, opcode[4]);
  and and_13 (and_13_out, not_26_out, not_27_out, not_28_out, not_29_out, not_30_out);
  and and_14 (and_14_out, opcode[1], opcode[2], opcode[3], not_31_out);
  and and_15 (SinalULA[2], opcode[0], not_32_out, not_33_out, not_34_out, not_35_out);
  and and_16 (SinalULA[0], opcode[0], not_36_out, opcode[2], not_37_out, not_38_out);
  and and_17 (SinalULA[3], not_39_out, opcode[1], not_40_out, not_41_out, not_42_out);
  and and_18 (SinalULA[4], opcode[0], opcode[1], not_43_out, not_44_out, not_45_out);
  and and_19 (SinalULA[5], not_46_out, not_47_out, opcode[2], not_48_out, not_49_out);
  and and_20 (SinalULA[7], not_50_out, opcode[1], not_51_out, opcode[3], not_52_out);
  and and_21 (SinalULA[8], opcode[0], opcode[1], not_53_out, opcode[3], not_54_out);
  and and_22 (SinalULA[9], not_55_out, not_56_out, opcode[2], opcode[3], not_57_out);
  and and_23 (SinalULA[12], opcode[0], opcode[1], opcode[2], not_58_out, not_59_out);
  and and_24 (SinalULA[11], not_60_out, opcode[1], opcode[2], not_61_out, not_62_out);
  and and_25 (SinalULA[10], not_63_out, not_64_out, not_65_out, opcode[3], not_66_out);
  and and_26 (SinalULA[6], opcode[0], not_67_out, not_68_out, opcode[3], not_69_out);
  nor nor_1 (isWb, and_7_out, and_8_out, and_9_out);
  xor xor_1 (isUbranch, and_10_out, and_11_out);
  xor xor_2 (SinalULA[1], and_13_out, and_14_out);
  // Pins of 1 and 13 bits meet at SinalULA

  assign isImm = in_3;

  // Other names for the same wires on the sheet: isAdd = SinalULA[1]; isAnd = SinalULA[11]; isAsr = SinalULA[9];
  //   isCmp = SinalULA[0]; isDiv = SinalULA[4]; isLsl = SinalULA[7]; isLsr = SinalULA[8]; isMod = SinalULA[5];
  //   isMov = SinalULA[6]; isMul = SinalULA[3]; isNot = SinalULA[10]; isOr = SinalULA[12]; isSub = SinalULA[2]
endmodule
