// Digital circuit controlpkt.dig as structural Verilog
module controlpkt (
  input  isRet,
  input  isBeq,
  input  [12:0] ALU_signals,
  input  isBgt,
  input  isUbranch,
  input  isLd,
  input  isSt,
  input  isCall,
  input  isWb,
  input  bubble,
  input  clkIn,
  output isret_o,
  output [12:0] ALU_o,
  output isbeq_o,
  output isbgt_o,
  output isub_o,
  output isld_o,
  output isst_o,
  output iscal_o,
  output iswb_o
);

  wire [7:0] multiplexer_2_out;
  wire [12:0] multiplexer_1_out;

  Register register_1 (.D(multiplexer_2_out[7]), .C(clkIn), .en(1'b1), .Q(isret_o));
  Multiplexer #(.Bits(13)) multiplexer_1 (.sel(bubble), .in_0(ALU_signals), .in_1({13{1'b0}}), .out(multiplexer_1_out));
  Register #(.Bits(13)) register_2 (.D(multiplexer_1_out), .C(clkIn), .en(1'b1), .Q(ALU_o));
  Register register_3 (.D(multiplexer_2_out[6]), .C(clkIn), .en(1'b1), .Q(isbeq_o));
  Register register_4 (.D(multiplexer_2_out[5]), .C(clkIn), .en(1'b1), .Q(isbgt_o));
  Register register_5 (.D(multiplexer_2_out[4]), .C(clkIn), .en(1'b1), .Q(isub_o));
  Multiplexer #(.Bits(8)) multiplexer_2 (
    .sel(bubble), .in_0({isRet, isBeq, isBgt, isUbranch, isLd, isSt, isCall, isWb}), .in_1({8{1'b0}}),
    .out(multiplexer_2_out));
  Register register_6 (.D(multiplexer_2_out[3]), .C(clkIn), .en(1'b1), .Q(isld_o));
  Register register_7 (.D(multiplexer_2_out[2]), .C(clkIn), .en(1'b1), .Q(isst_o));
  Register register_8 (.D(multiplexer_2_out[1]), .C(clkIn), .en(1'b1), .Q(iscal_o));
  Register register_9 (.D(multiplexer_2_out[0]), .C(clkIn), .en(1'b1), .Q(iswb_o));
endmodule
