// Digital circuit dflipflop.dig as structural Verilog
module dflipflop (
  input  D,
  input  clk,
  output Q,
  output Q_2
);

  wire and_1_out, and_2_out, not_1_out;

  and and_1 (and_1_out, not_1_out, clk);
  not not_1 (not_1_out, D);
  and and_2 (and_2_out, clk, D);
  nor nor_1 (Q, and_1_out, Q_2);
  nor nor_2 (Q_2, Q, and_2_out);
endmodule
