// Digital circuit flags.dig as structural Verilog
module flags (
  input  [3:0] isCmp,
  input  is_gt,
  input  is_eq,
  output flags_GT,
  output flags_E
);

  wire and_1_out;

  and and_1 (and_1_out, isCmp[0], ~isCmp[1], ~isCmp[2], ~isCmp[3]);  // And
  D_FF d_ff_1 (.D(is_gt), .C(and_1_out), .Q(flags_GT));  // open: nQ
  D_FF d_ff_2 (.D(is_eq), .C(and_1_out), .Q(flags_E));  // open: nQ
endmodule
