// Digital circuit forwarding-unit.dig as structural Verilog
module forwarding_unit (
  input  [31:0] MA_RW,
  input  [31:0] EX_MA,
  input  [31:0] OF_EX,
  input  [31:0] IF_OF,
  output RW_gt_MA_op2,
  output RW_gt_OF_op2,
  output RW_gt_OF_op1,
  output [1:0] RW_MA_gt_EX_op2,
  output [1:0] RW_MA_gt_EX_op1,
  output RW_gt_EX_op2
);

  wire and_1_out, conflit_detection_unit_2_fo_conflict;

  conflit_detection_unit conflit_detection_unit_1 (
    .A(MA_RW), .B(EX_MA), .FO_conflict(RW_gt_MA_op2));  // open: SO_conflict
  conflit_detection_unit conflit_detection_unit_2 (
    .A(EX_MA), .B(OF_EX), .FO_conflict(conflit_detection_unit_2_fo_conflict));  // open: SO_conflict
  and and_1 (and_1_out, OF_EX[27], OF_EX[28], OF_EX[29], OF_EX[30], ~OF_EX[31]);  // And
  Multiplexer multiplexer_1 (
    .sel(and_1_out), .in_0(conflit_detection_unit_2_fo_conflict), .in_1(1'b0), .out(RW_MA_gt_EX_op2[1]));
  conflit_detection_unit conflit_detection_unit_3 (
    .A(MA_RW), .B(OF_EX), .FO_conflict(RW_gt_EX_op2), .SO_conflict(RW_MA_gt_EX_op1[0]));
  Multiplexer multiplexer_2 (.sel(and_1_out), .in_0(RW_gt_EX_op2), .in_1(1'b0), .out(RW_MA_gt_EX_op2[0]));
  conflit_detection_unit conflit_detection_unit_4 (
    .A(MA_RW), .B(IF_OF), .FO_conflict(RW_gt_OF_op2), .SO_conflict(RW_gt_OF_op1));

  assign RW_MA_gt_EX_op1[1] = RW_gt_EX_op2;
endmodule
