// Digital circuit instruction-split-A.dig as structural Verilog
module instruction_split_A (
  input  [4:0] opA,
  input  [26:0] opA_A,
  output [3:0] src1,
  output has_src2,
  output [3:0] src2
);

  wire and_1_out, and_2_out, not_1_out;

  and and_1 (and_1_out, ~opA[0], ~opA[1], opA[2], ~opA[3], opA[4]);  // And
  Multiplexer #(.Bits(4)) multiplexer_1 (.sel(and_1_out), .in_0(opA_A[21:18]), .in_1(4'b1111), .out(src1));
  and and_2 (and_2_out, opA[0], opA[1], opA[2], opA[3], ~opA[4]);  // And
  not not_1 (not_1_out, opA_A[26]);
  Multiplexer multiplexer_2 (.sel(and_2_out), .in_0(not_1_out), .in_1(1'b1), .out(has_src2));
  Multiplexer #(.Bits(4)) multiplexer_3 (.sel(and_2_out), .in_0(opA_A[17:14]), .in_1(opA_A[25:22]), .out(src2));
endmodule
