// Digital circuit processor.dig as structural Verilog
module processor (
  input  in_1,
  input  clk
);

  wire clk_t, control_unit_1_isbeq, control_unit_1_isbgt, control_unit_1_iscall, control_unit_1_isimm,
       control_unit_1_isld, control_unit_1_isubranch, control_unit_1_iswb, data_lck_1_datalockconflict,
       ex_ma_1_iscall_o, ex_ma_1_isld_o, ex_ma_1_isst_o, ex_ma_1_iswb_o, flags_1_flags_e, flags_1_flags_gt,
       isBranchTaken, isRet, isSt, isWb, of_ex_1_p10, of_ex_1_p13, RW__gt_EX_op2, RW__gt_MA_op2,
       RW__gt_OF_op1, RW__gt_OF_op2, stall, ula_1_p5, ula_1_p6, undriven_7, undriven_8, undriven_9,
       undriven_10, undriven_11, undriven_12, undriven_13;
  wire [1:0] ma_rw_1_isld_o, RW_MA__gt_EX_op1, RW_MA__gt_EX_op2;
  wire [3:0] if_of_1_inst_out_2, multiplexer_3_out, multiplexer_4_out, of_ex_1_p12, \reg ;
  wire [12:0] control_unit_1_sinalula;
  wire [17:0] if_of_1_inst_out;
  wire [23:0] PC_q_2;
  wire [26:22] if_of_1_inst_out_3;
  wire [31:0] add_1_s, add_2_s, add_3_s, aluResult, barrelshifter_1_out, bitextender_1_out, branch_tgt,
       calculate_immediate_1_imm_x, data, ex_ma_1_instr_out, ex_ma_1_op2_out, ex_ma_1_pc_out,
       EX_MA_Instruction, if_of_1_pc_out, IF_OF_Instruction, ma_rw_1_alur_out, ma_rw_1_instr_out,
       ma_rw_1_loadr_out, ma_rw_1_pc_out, MA_RW_Instruction, multiplexer_1_out, multiplexer_2_out,
       multiplexer_5_out, multiplexer_6_out, multiplexer_7_out, multiplexer_8_out, multiplexer_9_out,
       multiplexer_10_out, multiplexer_12_out, OF_EX_Instruction, PC_q, ramdualport_1_d, registerfile_1_da,
       registerfile_1_db, rom_1_d, ula_1_p4, undriven, undriven_2, undriven_3, undriven_4, undriven_5,
       undriven_6;
  wire [31:27] if_of_1_inst_out_4;

  Multiplexer #(.Bits(32)) multiplexer_1 (
    .sel(isBranchTaken), .in_0(add_1_s), .in_1(branch_tgt), .out(multiplexer_1_out));
  Register #(.Bits(32)) PC (.D(multiplexer_1_out), .C(clk_t), .en(stall), .Q({PC_q[31:26], PC_q_2, PC_q[1:0]}));
  and and_1 (clk_t, in_1, clk);
  // Probe on {PC_q[31:26], PC_q_2, PC_q[1:0]}
  Add #(.Bits(32)) add_1 (.a({PC_q[31:26], PC_q_2, PC_q[1:0]}), .b(32'h4), .c_i(1'b0), .s(add_1_s));  // open: c_o
  Data_Lck data_lck_1 (
    .IF_OF(IF_OF_Instruction), .OF_EX(OF_EX_Instruction), .DataLockConflict(data_lck_1_datalockconflict));
  // forwarding_unit forwarding_unit_1: pin names not known; wires that end beside it: MA_RW_Instruction, EX_MA_Instruction, OF_EX_Instruction, IF_OF_Instruction, RW__gt_MA_op2, RW__gt_OF_op1, RW__gt_OF_op2, RW_MA__gt_EX_op2, RW_MA__gt_EX_op1, RW__gt_EX_op2
  ROM #(.AddrBits(24), .Bits(32)) rom_1 (.A(PC_q_2), .sel(1'b1), .D(rom_1_d));
  not not_1 (stall, data_lck_1_datalockconflict);
  Multiplexer #(.Bits(32)) multiplexer_2 (
    .sel(isBranchTaken), .in_0(rom_1_d), .in_1(32'h68000000), .out(multiplexer_2_out));
  IF_OF if_of_1 (
    .stall(stall), .PC({PC_q[31:26], PC_q_2, PC_q[1:0]}), .Inst(multiplexer_2_out), .clkIn(clk_t),
    .bubble(IF_OF_Instruction), .Pc_out(if_of_1_pc_out),
    .Inst_out({if_of_1_inst_out_4, if_of_1_inst_out_3, if_of_1_inst_out_2, if_of_1_inst_out}));
  control_unit control_unit_1 (
    .opcode(if_of_1_inst_out_4), .I_bit(if_of_1_inst_out_3[26]), .isSt(isSt), .isImm(control_unit_1_isimm),
    .isLd(control_unit_1_isld), .isBeq(control_unit_1_isbeq), .isBgt(control_unit_1_isbgt), .isRet(isRet),
    .isWb(control_unit_1_iswb), .isUbranch(control_unit_1_isubranch), .isCall(control_unit_1_iscall),
    .SinalULA(control_unit_1_sinalula));
  Multiplexer #(.Bits(4)) multiplexer_3 (
    .sel(isRet), .in_0(if_of_1_inst_out_2), .in_1(4'b1111), .out(multiplexer_3_out));
  Multiplexer #(.Bits(4)) multiplexer_4 (
    .sel(isSt), .in_0(if_of_1_inst_out[17:14]), .in_1(if_of_1_inst_out_3[25:22]), .out(multiplexer_4_out));
  BitExtender #(.inputBits(27), .outputBits(32)) bitextender_1 (
    .in({if_of_1_inst_out_3, if_of_1_inst_out_2, if_of_1_inst_out}), .out(bitextender_1_out));
  calculate_immediate calculate_immediate_1 (.imm(if_of_1_inst_out), .imm_x(calculate_immediate_1_imm_x));
  BarrelShifter #(.Bits(32)) barrelshifter_1 (.in(bitextender_1_out), .shift(6'b000010), .out(barrelshifter_1_out));
  RegisterFile #(.AddrBits(4), .Bits(32)) registerfile_1 (
    .Din(data), .we(isWb), .Rw(\reg ), .C(clk_t), .Ra(multiplexer_3_out), .Rb(multiplexer_4_out),
    .Da(registerfile_1_da), .Db(registerfile_1_db));
  Multiplexer #(.Bits(32)) multiplexer_5 (
    .sel(control_unit_1_isimm), .in_0(multiplexer_7_out), .in_1(calculate_immediate_1_imm_x),
    .out(multiplexer_5_out));
  Add #(.Bits(32)) add_2 (.a(barrelshifter_1_out), .b(if_of_1_pc_out), .c_i(1'b0), .s(add_2_s));  // open: c_o
  Multiplexer #(.Bits(32)) multiplexer_6 (
    .sel(RW__gt_OF_op1), .in_0(registerfile_1_da), .in_1(data), .out(multiplexer_6_out));
  Multiplexer #(.Bits(32)) multiplexer_7 (
    .sel(RW__gt_OF_op2), .in_0(registerfile_1_db), .in_1(data), .out(multiplexer_7_out));
  // Probe on multiplexer_7_out
  // OF_EX of_ex_1: pin names not known; wires that end beside it: isSt, control_unit_1_iscall, control_unit_1_iswb, {if_of_1_inst_out_4, if_of_1_inst_out_3, if_of_1_inst_out_2, if_of_1_inst_out}, if_of_1_pc_out, add_2_s, multiplexer_5_out, multiplexer_6_out, multiplexer_7_out, of_ex_1_p10, clk_t, of_ex_1_p12, of_ex_1_p13
  or or_1 (of_ex_1_p10, ~stall, isBranchTaken);  // Or
  Multiplexer #(.Bits(32)) multiplexer_8 (.sel(RW__gt_EX_op2), .in_0(undriven_5), .in_1(data), .out(multiplexer_8_out));
  Multiplexer #(.Selector_Bits(2), .Bits(32)) multiplexer_9 (
    .sel(RW_MA__gt_EX_op1), .in_0(undriven_4), .in_1(data), .in_2(aluResult), .in_3(aluResult),
    .out(multiplexer_9_out));
  Multiplexer #(.Selector_Bits(2), .Bits(32)) multiplexer_10 (
    .sel(RW_MA__gt_EX_op2), .in_0(undriven_3), .in_1(data), .in_2(aluResult), .in_3(aluResult),
    .out(multiplexer_10_out));
  Multiplexer #(.Bits(32)) multiplexer_11 (
    .sel(of_ex_1_p13), .in_0(undriven_2), .in_1(multiplexer_9_out), .out(branch_tgt));
  Branch_Unit branch_unit_1 (
    .isUBranch(undriven_11), .isBEQ(undriven_12), .flags_E(flags_1_flags_e), .isBgt(undriven_13),
    .flags_GT(flags_1_flags_gt), .isBrachTaken(isBranchTaken));
  flags flags_1 (
    .is_gt(ula_1_p5), .isCmp(of_ex_1_p12), .is_eq(ula_1_p6), .flags_GT(flags_1_flags_gt),
    .flags_E(flags_1_flags_e));
  // ula ula_1: pin names not known; wires that end beside it: multiplexer_9_out, multiplexer_10_out, of_ex_1_p12, ula_1_p4, ula_1_p5, ula_1_p6
  EX_MA ex_ma_1 (
    .PC(undriven), .aluR(ula_1_p4), .op2(multiplexer_8_out), .instr(undriven_6), .isld(undriven_7),
    .isst(undriven_8), .iscall(undriven_9), .iswb(undriven_10), .clkIn(clk_t),
    .instr_out2(EX_MA_Instruction), .PC_out(ex_ma_1_pc_out), .aluR_out(aluResult), .op2_out(ex_ma_1_op2_out),
    .instr_out(ex_ma_1_instr_out), .iswb_o(ex_ma_1_iswb_o), .iscall_o(ex_ma_1_iscall_o),
    .isst_o(ex_ma_1_isst_o), .isld_o(ex_ma_1_isld_o));
  Multiplexer #(.Bits(32)) multiplexer_12 (
    .sel(RW__gt_MA_op2), .in_0(ex_ma_1_op2_out), .in_1(data), .out(multiplexer_12_out));
  RAMDualPort #(.AddrBits(24), .Bits(32)) ramdualport_1 (
    .A(aluResult[25:2]), .Din(multiplexer_12_out), .str(ex_ma_1_isst_o), .C(clk_t), .ld(ex_ma_1_isld_o),
    .D(ramdualport_1_d));
  MA_RW ma_rw_1 (
    .PC(ex_ma_1_pc_out), .loadR(ramdualport_1_d), .aluR(aluResult), .instr(ex_ma_1_instr_out),
    .isld(ex_ma_1_isld_o), .iscall(ex_ma_1_iscall_o), .iswb(ex_ma_1_iswb_o), .clkIn(clk_t),
    .instr_out2(MA_RW_Instruction), .PC_out(ma_rw_1_pc_out), .loadR_out(ma_rw_1_loadr_out),
    .aluR_out(ma_rw_1_alur_out), .instr_out(ma_rw_1_instr_out), .iswb_o(isWb), .iscall_o(ma_rw_1_isld_o[1]),
    .isld_o(ma_rw_1_isld_o[0]));
  Multiplexer #(.Bits(4)) multiplexer_13 (
    .sel(ma_rw_1_isld_o[1]), .in_0(ma_rw_1_instr_out[25:22]), .in_1(4'b1111), .out(\reg ));
  Add #(.Bits(32)) add_3 (.a(ma_rw_1_pc_out), .b(32'h4), .c_i(1'b0), .s(add_3_s));  // open: c_o
  Multiplexer #(.Selector_Bits(2), .Bits(32)) multiplexer_14 (
    .sel(ma_rw_1_isld_o), .in_0(ma_rw_1_alur_out), .in_1(ma_rw_1_loadr_out), .in_2(add_3_s),
    .in_3({32{1'b0}}), .out(data));
  // Probe on data

  // Notes on the sheet:
  //   clk: Hz: 10
  //   contents of rom_1 (hex, n*v repeats v):
  //   0,4c400000,4c800014,4cc00001,4d000001,98000002,68000000,7cc40000
  //   ,7d040004,4d400002,28148000,8800000f,e540001,56a40002,2468000
  //   ,75a40000,e540002,56a40002,2468000,75e40000,219c000,56540002,2464000
  //   ,7e240000,5540001,97fffff1,a0000000
  //   Memory Unit
endmodule
