// Digital circuit ula.dig as structural Verilog
module ula (
  input  [31:0] B,
  input  [31:0] A,
  input  [3:0] ula_control,
  output [31:0] \output ,
  output branch
);

  wire and_3_out, comparator_1_gt, eq, lt, multiplexer_7_out, nor_1_out, not_1_out, or_2_out;
  wire [31:0] in_0, in_1, in_2, in_3, in_4, in_6, in_7, in_8, in_9, in_12, in_13;

  Add #(.Bits(32)) add_addi (.a(A), .b(B), .c_i(1'b0), .s(in_0));  // open: c_o
  BarrelShifter #(.Bits(32)) sll_slli (.in(B), .shift(A[5:0]), .out(in_1));
  Comparator #(.Bits(32)) comparator_1 (.a(A), .b(B), .gt(comparator_1_gt), .eq(eq), .lt(lt));
  assign in_4 = A ^ B;  // XOr xor_1, 32 bits wide
  assign in_6 = A | B;  // Or or_1, 32 bits wide
  assign in_7 = A & B;  // And and_1, 32 bits wide
  Sub #(.Bits(32)) sub (.a(B), .b(A), .c_i(1'b0), .s(in_3));  // open: c_o
  not not_1 (not_1_out, eq);
  Multiplexer #(.Bits(32)) multiplexer_1 (.sel(lt), .in_0({32{1'b0}}), .in_1(32'h1), .out(in_2));
  Multiplexer #(.Bits(32)) multiplexer_2 (.sel(eq), .in_0({32{1'b0}}), .in_1(32'h1), .out(in_8));
  or or_2 (or_2_out, comparator_1_gt, eq);
  Multiplexer #(.Bits(32)) multiplexer_3 (.sel(not_1_out), .in_0({32{1'b0}}), .in_1(32'h1), .out(in_9));
  Multiplexer #(.Bits(32)) multiplexer_4 (.sel(lt), .in_0({32{1'b0}}), .in_1(32'h1), .out(in_12));
  Multiplexer #(.Bits(32)) multiplexer_5 (.sel(or_2_out), .in_0({32{1'b0}}), .in_1(32'h1), .out(in_13));
  Multiplexer #(.Selector_Bits(4), .Bits(32)) multiplexer_6 (
    .sel(ula_control), .in_0(in_0), .in_1(in_1), .in_2(in_2), .in_3(in_3), .in_4(in_4), .in_5({32{1'b0}}),
    .in_6(in_6), .in_7(in_7), .in_8(in_8), .in_9(in_9), .in_10({32{1'b0}}), .in_11({32{1'b0}}),
    .in_12(in_12), .in_13(in_13), .in_14({32{1'b0}}), .in_15(B), .out(\output ));
  Multiplexer multiplexer_7 (.sel(ula_control[3]), .in_0(1'b0), .in_1(1'b1), .out(multiplexer_7_out));
  nor nor_1 (nor_1_out, \output [1], \output [2], \output [3], \output [4], \output [5], \output [6], \output [7], \output [8], \output [9], \output [10], \output [11], \output [12], \output [13], \output [14], \output [15], \output [16], \output [17], \output [18], \output [19], \output [20], \output [21], \output [22], \output [23], \output [24], \output [25], \output [26], \output [27], \output [28], \output [29], \output [30], \output [31]);
  and and_2 (branch, multiplexer_7_out, and_3_out);
  and and_3 (and_3_out, \output [0], nor_1_out);

  // Notes on the sheet:
  //   xor/xori
  //   or/ori
  //   and,andi
  //   jal/jalr
  //   slt/slti
  //   bne
  //   beq
  //   blt
  //   bge
endmodule
