// Digital circuit IF_OF.dig as structural Verilog
module IF_OF (
  input  stall,
  input  clkIn,
  input  [31:0] PC,
  input  [31:0] Inst,
  output [31:0] Pc_out,
  output [31:0] Inst_out,
  output [31:0] bubble
);

  Register #(.Bits(32)) register_1 (.D(PC), .C(clkIn), .en(stall), .Q(Pc_out));
  Register #(.Bits(32)) register_2 (.D(Inst), .C(clkIn), .en(stall), .Q(bubble));

  assign Inst_out = bubble;
endmodule
