// Digital circuit MA_RW.dig as structural Verilog
module MA_RW (
  input  [31:0] PC,
  input  [31:0] loadR,
  input  [31:0] aluR,
  input  [31:0] instr,
  input  clkIn,
  input  isld,
  input  iscall,
  input  iswb,
  output [31:0] PC_out,
  output [31:0] loadR_out,
  output [31:0] aluR_out,
  output [31:0] instr_out,
  output iswb_o,
  output iscall_o,
  output isld_o,
  output [31:0] instr_out2
);

  Register #(.Bits(32)) register_1 (.D(PC), .C(clkIn), .en(1'b1), .Q(PC_out));
  Register #(.Bits(32)) register_2 (.D(loadR), .C(clkIn), .en(1'b1), .Q(loadR_out));
  Register #(.Bits(32)) register_3 (.D(aluR), .C(clkIn), .en(1'b1), .Q(aluR_out));
  Register #(.Bits(32)) register_4 (.D(instr), .C(clkIn), .en(1'b1), .Q(instr_out));
  Register register_5 (.D(isld), .C(clkIn), .en(1'b1), .Q(isld_o));
  Register register_6 (.D(iscall), .C(clkIn), .en(1'b1), .Q(iscall_o));
  Register register_7 (.D(iswb), .C(clkIn), .en(1'b1), .Q(iswb_o));

  assign instr_out2 = instr_out;
endmodule
