// Digital circuit calculate_immediate.dig as structural Verilog
module calculate_immediate (
  input  [17:0] imm,
  output [31:0] imm_x
);

  wire [31:0] barrelshifter_1_out, bitextender_1_out, bitextender_2_out;

  BitExtender #(.inputBits(16), .outputBits(32)) bitextender_1 (.in(imm[15:0]), .out(bitextender_1_out));
  BitExtender #(.inputBits(16), .outputBits(32)) bitextender_2 (.in(imm[15:0]), .out(bitextender_2_out));
  BarrelShifter #(.Bits(32)) barrelshifter_1 (.in(bitextender_1_out), .shift(6'b010000), .out(barrelshifter_1_out));
  Multiplexer #(.Selector_Bits(2), .Bits(32)) multiplexer_1 (
    .sel(imm[17:16]), .in_0(bitextender_2_out), .in_1(bitextender_1_out), .in_2(barrelshifter_1_out),
    .in_3({32{1'b0}}), .out(imm_x));
endmodule
