// Digital circuit check-opB.dig as structural Verilog
module check_opB (
  input  [4:0] I,
  output O
);

  wire and_1_out, and_2_out, and_3_out, and_4_out, and_5_out;

  and and_1 (and_1_out, I[0], ~I[1], I[2], ~I[4]);  // And
  and and_2 (and_2_out, I[0], I[2], I[3], ~I[4]);  // And
  nor nor_1 (O, and_5_out, and_4_out, and_3_out, and_2_out, and_1_out);
  and and_3 (and_3_out, ~I[1], ~I[2], ~I[3], I[4]);  // And
  and and_4 (and_4_out, ~I[0], ~I[2], ~I[3], I[4]);  // And
  and and_5 (and_5_out, ~I[0], ~I[1], ~I[3], I[4]);  // And
endmodule
