// Digital circuit instruction-split-b.dig as structural Verilog
module instruction_split_b (
  input  [4:0] opB_5,
  input  [26:0] opB_27,
  output [3:0] dest
);

  wire and_1_out;

  and and_1 (and_1_out, opB_5[0], opB_5[1], ~opB_5[2], ~opB_5[3], opB_5[4]);  // And
  Multiplexer #(.Bits(4)) multiplexer_1 (.sel(and_1_out), .in_0(opB_27[25:22]), .in_1(4'b1111), .out(dest));
endmodule
