// Digital circuit previsor_desvios.dig as structural Verilog
module previsor_desvios (
  input  T,
  input  clk,
  output P
);

  wire and_1_out, and_2_out, and_3_out, and_4_out, and_5_out, and_6_out, and_7_out, and_8_out, not_1_out,
       not_2_out, not_3_out;
  wire [0:0] or_1_out;
  wire [1:0] register_1_q;

  Register #(.Bits(2)) register_1 (.D({P, or_1_out[0]}), .C(clk), .en(1'b1), .Q(register_1_q));
  not not_1 (not_1_out, register_1_q[0]);
  not not_2 (not_2_out, register_1_q[1]);
  not not_3 (not_3_out, T);
  and and_1 (and_1_out, not_1_out, not_2_out, T);
  and and_2 (and_2_out, register_1_q[0], not_2_out, not_3_out);
  and and_3 (and_3_out, not_1_out, register_1_q[1], not_3_out);
  and and_4 (and_4_out, register_1_q[0], not_2_out, T);
  and and_5 (and_5_out, not_1_out, register_1_q[1], register_1_q[1], not_3_out, T);
  and and_6 (and_6_out, register_1_q[0], not_2_out, T);
  and and_7 (and_7_out, not_1_out, register_1_q[1], not_3_out);
  and and_8 (and_8_out, register_1_q[1], T);
  or or_1 (or_1_out[0], and_1_out, and_2_out, and_3_out);
  or or_2 (P, and_4_out, and_5_out, and_6_out, and_7_out, and_8_out);
endmodule
