// Digital circuit processor.dig as structural Verilog
module processor (
  input  in_1,
  input  clk,
  input  rst
);

  wire and_1_out, and_3_out, clk_t, comp_eq, comp_gt, control_unit_1_isbeq, control_unit_1_isbgt,
       control_unit_1_iscall, control_unit_1_isimm, control_unit_1_isld, control_unit_1_isubranch,
       control_unit_1_iswb, data_lck_1_datalockconflict, dflipflop_1_q, dflipflop_2_q, err, err2, ex_ma_1_p1,
       EX_MA_Instruction, isBranchTaken, isPrevRight, isRet, isSt, isWb, of_ex_1_p10, of_ex_1_p13,
       previsao_q, previsor_desvios_1_p, register_2_q, register_5_q, RW__gt_EX_op2, RW__gt_MA_op2,
       RW__gt_OF_op1, RW__gt_OF_op2, stall, ula_1_p4, undriven_5, undriven_6, undriven_7, undriven_8,
       undriven_10, undriven_12, undriven_13, xnor_1_out;
  wire [1:0] ma_rw_1_isld_o, RW_MA__gt_EX_op1, RW_MA__gt_EX_op2;
  wire [3:0] control_unit_1_sinalula, if_of_1_inst_out_2, multiplexer_4_out, multiplexer_5_out, of_ex_1_p12,
       \reg ;
  wire [17:0] if_of_1_inst_out;
  wire [26:22] if_of_1_inst_out_3;
  wire [31:0] add_1_s, add_2_s, add_3_s, aluResult, barrelshifter_1_out, bitextender_1_out, branch_tgt,
       calculate_immediate_1_imm_x, data, ex_ma_1_p5, if_of_1_pc_out, IF_OF_Instruction, ma_rw_1_alur_out,
       ma_rw_1_instr_out, ma_rw_1_loadr_out, ma_rw_1_pc_out, MA_RW_Instruction, multiplexer_1_out,
       multiplexer_2_out, multiplexer_3_out, multiplexer_6_out, multiplexer_7_out, multiplexer_8_out,
       multiplexer_9_out, multiplexer_10_out, multiplexer_11_out, multiplexer_13_out, OF_EX_Instruction,
       PC_q, ramdualport_1_d, register_3_q, register_4_q, registerfile_1_da, registerfile_1_db, rom_1_d,
       undriven, undriven_2, undriven_3, undriven_4, undriven_9, undriven_11;
  wire [31:27] if_of_1_inst_out_4;

  xnor xnor_1 (xnor_1_out, isBranchTaken, previsor_desvios_1_p);
  Register register_1 (.D(register_2_q), .C(clk_t), .en(1'b1), .Q(err));
  and and_1 (and_1_out, stall, xnor_1_out);
  Register register_2 (.D(err2), .C(clk_t), .en(1'b1), .Q(register_2_q));
  previsor_desvios previsor_desvios_1 (.T(isBranchTaken), .clk(clk_t), .P(previsor_desvios_1_p));
  // Probe on multiplexer_1_out
  not not_1 (err2, and_1_out);
  Multiplexer #(.Bits(32)) multiplexer_1 (
    .sel(previsor_desvios_1_p), .in_0(multiplexer_3_out), .in_1(multiplexer_2_out), .out(multiplexer_1_out));
  Register #(.Bits(32)) PC (.D(multiplexer_1_out), .C(clk_t), .en(and_1_out), .Q(PC_q));
  and and_2 (clk_t, clk, in_1);
  Multiplexer #(.Bits(32)) multiplexer_2 (.sel(err), .in_0(branch_tgt), .in_1(register_3_q), .out(multiplexer_2_out));
  Multiplexer #(.Bits(32)) multiplexer_3 (.sel(err), .in_0(add_1_s), .in_1(PC_q), .out(multiplexer_3_out));
  // Probe on PC_q
  // Probe on multiplexer_2_out
  // Probe on register_3_q
  Data_Lck data_lck_1 (
    .IF_OF(IF_OF_Instruction), .OF_EX(OF_EX_Instruction), .DataLockConflict(data_lck_1_datalockconflict));
  // forwarding_unit forwarding_unit_1: pin names not known; wires that end beside it: MA_RW_Instruction, EX_MA_Instruction, OF_EX_Instruction, IF_OF_Instruction, RW__gt_MA_op2, RW__gt_OF_op1, RW__gt_OF_op2, RW_MA__gt_EX_op2, RW_MA__gt_EX_op1, RW__gt_EX_op2
  Register #(.Bits(32)) register_3 (.D(register_4_q), .C(clk_t), .en(1'b1), .Q(register_3_q));
  Add #(.Bits(32)) add_1 (.a(PC_q), .b(32'h4), .c_i(1'b0), .s(add_1_s));  // open: c_o
  Register #(.Bits(32)) register_4 (.D(branch_tgt), .C(clk_t), .en(1'b1), .Q(register_4_q));
  ROM #(.AddrBits(24), .Bits(32)) rom_1 (.A(PC_q[25:2]), .sel(1'b1), .D(rom_1_d));
  not not_2 (stall, data_lck_1_datalockconflict);
  Register previsao (.D(previsor_desvios_1_p), .C(clk_t), .en(1'b1), .Q(previsao_q));
  IF_OF if_of_1 (
    .stall(and_1_out), .PC(PC_q), .Inst(rom_1_d), .clkIn(clk_t), .bubble(IF_OF_Instruction),
    .Pc_out(if_of_1_pc_out),
    .Inst_out({if_of_1_inst_out_4, if_of_1_inst_out_3, if_of_1_inst_out_2, if_of_1_inst_out}));
  control_unit control_unit_1 (
    .opcode(if_of_1_inst_out_4), .I_bit(if_of_1_inst_out_3[26]), .isSt(isSt), .isImm(control_unit_1_isimm),
    .isLd(control_unit_1_isld), .isBeq(control_unit_1_isbeq), .isBgt(control_unit_1_isbgt), .isRet(isRet),
    .isWb(control_unit_1_iswb), .isUbranch(control_unit_1_isubranch), .isCall(control_unit_1_iscall),
    .SinalULA(control_unit_1_sinalula));
  Multiplexer #(.Bits(4)) multiplexer_4 (
    .sel(isRet), .in_0(if_of_1_inst_out_2), .in_1(4'b1111), .out(multiplexer_4_out));
  Multiplexer #(.Bits(4)) multiplexer_5 (
    .sel(isSt), .in_0(if_of_1_inst_out[17:14]), .in_1(if_of_1_inst_out_3[25:22]), .out(multiplexer_5_out));
  BitExtender #(.inputBits(27), .outputBits(32)) bitextender_1 (
    .in({if_of_1_inst_out_3, if_of_1_inst_out_2, if_of_1_inst_out}), .out(bitextender_1_out));
  calculate_immediate calculate_immediate_1 (.imm(if_of_1_inst_out), .imm_x(calculate_immediate_1_imm_x));
  BarrelShifter #(.Bits(32)) barrelshifter_1 (.in(bitextender_1_out), .shift(6'b000010), .out(barrelshifter_1_out));
  RegisterFile #(.AddrBits(4), .Bits(32)) registerfile_1 (
    .Din(data), .we(isWb), .Rw(\reg ), .C(clk_t), .Ra(multiplexer_4_out), .Rb(multiplexer_5_out),
    .Da(registerfile_1_da), .Db(registerfile_1_db));
  Multiplexer #(.Bits(32)) multiplexer_6 (
    .sel(control_unit_1_isimm), .in_0(multiplexer_8_out), .in_1(calculate_immediate_1_imm_x),
    .out(multiplexer_6_out));
  Add #(.Bits(32)) add_2 (.a(barrelshifter_1_out), .b(if_of_1_pc_out), .c_i(1'b0), .s(add_2_s));  // open: c_o
  Multiplexer #(.Bits(32)) multiplexer_7 (
    .sel(RW__gt_OF_op1), .in_0(registerfile_1_da), .in_1(data), .out(multiplexer_7_out));
  Multiplexer #(.Bits(32)) multiplexer_8 (
    .sel(RW__gt_OF_op2), .in_0(registerfile_1_db), .in_1(data), .out(multiplexer_8_out));
  // Probe on multiplexer_8_out
  Register register_5 (.D(previsao_q), .C(clk_t), .en(1'b1), .Q(register_5_q));
  // OF_EX of_ex_1: pin names not known; wires that end beside it: isSt, control_unit_1_iscall, control_unit_1_iswb, {if_of_1_inst_out_4, if_of_1_inst_out_3, if_of_1_inst_out_2, if_of_1_inst_out}, if_of_1_pc_out, add_2_s, multiplexer_6_out, multiplexer_7_out, multiplexer_8_out, of_ex_1_p10, clk_t, of_ex_1_p12, of_ex_1_p13
  or or_1 (of_ex_1_p10, ~stall, ~isPrevRight);  // Or
  Multiplexer #(.Bits(32)) multiplexer_9 (.sel(RW__gt_EX_op2), .in_0(undriven_4), .in_1(data), .out(multiplexer_9_out));
  Multiplexer #(.Selector_Bits(2), .Bits(32)) multiplexer_10 (
    .sel(RW_MA__gt_EX_op1), .in_0(undriven_3), .in_1(data), .in_2(aluResult), .in_3(aluResult),
    .out(multiplexer_10_out));
  Multiplexer #(.Selector_Bits(2), .Bits(32)) multiplexer_11 (
    .sel(RW_MA__gt_EX_op2), .in_0(undriven_2), .in_1(data), .in_2(aluResult), .in_3(aluResult),
    .out(multiplexer_11_out));
  xnor xnor_2 (isPrevRight, isBranchTaken, register_5_q);
  Multiplexer #(.Bits(32)) multiplexer_12 (
    .sel(of_ex_1_p13), .in_0(undriven), .in_1(multiplexer_10_out), .out(branch_tgt));
  Branch_Unit branch_unit_1 (
    .isUBranch(undriven_5), .isBEQ(undriven_6), .flags_E(dflipflop_2_q), .isBgt(undriven_7),
    .flags_GT(dflipflop_1_q), .isBrachTaken(isBranchTaken));
  Comparator #(.Signed("true"), .Bits(32)) comp (
    .a(multiplexer_10_out), .b(multiplexer_11_out), .gt(comp_gt), .eq(comp_eq));  // open: lt
  // ula ula_1: pin names not known; wires that end beside it: multiplexer_10_out, multiplexer_11_out, of_ex_1_p12, ula_1_p4
  and and_3 (and_3_out, of_ex_1_p12[0], ~of_ex_1_p12[1], ~of_ex_1_p12[2], ~of_ex_1_p12[3]);  // And
  // EX_MA ex_ma_1: pin names not known; wires that end beside it: ex_ma_1_p1, ula_1_p4, multiplexer_9_out, EX_MA_Instruction, ex_ma_1_p5, aluResult
  dflipflop dflipflop_1 (.D(comp_gt), .clk(and_3_out), .rst(rst), .Q(dflipflop_1_q));  // open: Q_2
  dflipflop dflipflop_2 (.D(comp_eq), .clk(and_3_out), .rst(rst), .Q(dflipflop_2_q));  // open: Q_2
  Multiplexer #(.Bits(32)) multiplexer_13 (
    .sel(RW__gt_MA_op2), .in_0(undriven_9), .in_1(data), .out(multiplexer_13_out));
  RAMDualPort #(.AddrBits(24), .Bits(32)) ramdualport_1 (
    .A(aluResult[25:2]), .Din(multiplexer_13_out), .str(undriven_12), .C(clk_t), .ld(undriven_13),
    .D(ramdualport_1_d));
  MA_RW ma_rw_1 (
    .PC(ex_ma_1_p5), .loadR(ramdualport_1_d), .aluR(aluResult), .instr(undriven_11), .isld(undriven_13),
    .iscall(undriven_10), .iswb(undriven_8), .clkIn(clk_t), .instr_out2(MA_RW_Instruction),
    .PC_out(ma_rw_1_pc_out), .loadR_out(ma_rw_1_loadr_out), .aluR_out(ma_rw_1_alur_out),
    .instr_out(ma_rw_1_instr_out), .iswb_o(isWb), .iscall_o(ma_rw_1_isld_o[1]), .isld_o(ma_rw_1_isld_o[0]));
  Multiplexer #(.Bits(4)) multiplexer_14 (
    .sel(ma_rw_1_isld_o[1]), .in_0(ma_rw_1_instr_out[25:22]), .in_1(4'b1111), .out(\reg ));
  Add #(.Bits(32)) add_3 (.a(ma_rw_1_pc_out), .b(32'h4), .c_i(1'b0), .s(add_3_s));  // open: c_o
  Multiplexer #(.Selector_Bits(2), .Bits(32)) multiplexer_15 (
    .sel(ma_rw_1_isld_o), .in_0(ma_rw_1_alur_out), .in_1(ma_rw_1_loadr_out), .in_2(add_3_s),
    .in_3({32{1'b0}}), .out(data));
  // Probe on data

  // Notes on the sheet:
  //   clk: Hz: 10
  //   contents of rom_1 (hex, n*v repeats v):
  //   0,4c400000,4c800014,4cc00001,4d000001,98000002,68000000,7cc40000
  //   ,7d040004,4d400002,28148000,8800000f,e540001,56a40002,2468000
  //   ,75a40000,e540002,56a40002,2468000,75e40000,219c000,56540002,2464000
  //   ,7e240000,5540001,97fffff1,a0000000
  //   Flags
  //   Memory Unit
endmodule
