// Digital circuit registradores_pipeline.dig as structural Verilog
module registradores_pipeline (
);

  OF_EX of_ex ();  // open: Inst, PC, brantgt, B, A, OP2, bubble, clkIn, Inst_out2, PC_out, brantgt_out, B_out, A_out, OP2_out, Inst_out, isWb, isCall, isSt, isLd, isUbranch, isBgt, ALU_signals, isBeq, isRet, isret_out, aluSignals_out, isbeq_out, isgbt_out, isub_out, isld_out, isst_out, iscal_out, iswb_out
  EX_MA ex_ma_1 ();  // open: PC, aluR, op2, instr, isld, isst, iscall, iswb, clkIn, instr_out2, PC_out, aluR_out, op2_out, instr_out, iswb_o, iscall_o, isst_o, isld_o
  MA_RW ma_rw_1 ();  // open: PC, loadR, aluR, instr, isld, iscall, iswb, clkIn, instr_out2, PC_out, loadR_out, aluR_out, instr_out, iswb_o, iscall_o, isld_o
  IF_OF if_of ();  // open: stall, PC, Inst, clkIn, bubble, Pc_out, Inst_out

  // Notes on the sheet:
  //   IF/OF
  //   OF/EX
  //   EX/MA
  //   MA/RW
endmodule
