// Digital circuit check-opA-op1.dig as structural Verilog
module check_opA_op1 (
  input  [4:0] I,
  output O
);

  wire and_1_out, and_2_out, and_3_out;

  and and_1 (and_1_out, ~I[2], ~I[3], I[4]);  // And
  and and_2 (and_2_out, I[0], ~I[1], I[2], I[3], ~I[4]);  // And
  nor nor_1 (O, and_3_out, and_2_out, and_1_out);
  and and_3 (and_3_out, ~I[1], ~I[1], I[3], ~I[4]);  // And
endmodule
