// Digital circuit dflipflop.dig as structural Verilog
module dflipflop (
  input  D,
  input  clk,
  input  rst,
  output Q,
  output Q_2
);

  wire and_1_out, and_2_out, and_3_out, not_1_out, not_2_out, or_1_out;

  not not_1 (not_1_out, rst);
  and and_1 (and_1_out, D, not_1_out);
  or or_1 (or_1_out, clk, rst);
  and and_2 (and_2_out, not_2_out, or_1_out);
  not not_2 (not_2_out, and_1_out);
  and and_3 (and_3_out, or_1_out, and_1_out);
  nor nor_1 (Q, and_2_out, Q_2);
  nor nor_2 (Q_2, Q, and_3_out);
endmodule
